// Logisim project Exercicio-2.circ as structural Verilog: 1 circuit, main circuit main
module main (
  input  A,
  input  B,
  input  A_2,
  input  B_2,
  output out_5,
  output out_6
);

  wire and_1_out, and_2_out, not_1_out, not_2_out;

  not not_1 (not_1_out, A);
  not not_2 (not_2_out, B);
  xor xor_1 (out_6, A_2, B_2);
  and and_1 (and_1_out, not_1_out, B);
  and and_2 (and_2_out, A, not_2_out);
  or or_1 (out_5, and_1_out, and_2_out);

  // Notes on the sheet:
  //   A_2: pull=down
  //   Ou-Exclusivo
  //   Essa é a verdadeira porta logica Ou-Exclusivo.
  //   É uma possivel representação para a porta logica do Ou-Exclusivo. Utilizando NOT, AND e OR.
  //   Ela só funciona se apenas uma das entradas estiverem ativas(ou A, ou B, mas nunca as duas juntas).
endmodule
