// Logisim project Exercicio-1.circ as structural Verilog: 1 circuit, main circuit main
module main (
  input  A,
  input  B,
  input  C,
  input  A_2,
  input  B_2,
  input  C_2,
  input  A_3,
  input  B_3,
  input  C_3,
  input  D,
  input  W,
  input  X,
  input  Y,
  output S,
  output S_2,
  output S_3,
  output Z
);

  wire and_1_out, and_2_out, and_3_out, and_4_out, and_5_out, not_1_out, not_2_out, not_3_out, not_4_out,
       not_5_out, not_6_out, or_1_out, or_2_out, or_3_out;

  not not_1 (not_1_out, B);
  not not_2 (not_2_out, Y);
  or or_1 (or_1_out, A, B);
  or or_2 (or_2_out, not_1_out, C);
  and and_1 (and_1_out, B_2, C_2, not_3_out);
  not not_3 (not_3_out, A_2);
  and and_2 (and_2_out, B_2, C_2);
  and and_3 (and_3_out, A_2, C_2);
  and and_4 (and_4_out, A_3, B_3);
  not not_4 (not_4_out, C_3);
  and and_5 (and_5_out, C_3, D);
  not not_5 (not_5_out, and_5_out);
  or or_3 (or_3_out, W, not_2_out);
  and and_6 (S, or_1_out, or_2_out);
  not not_6 (not_6_out, and_2_out);
  or or_4 (S_3, and_4_out, not_4_out, not_5_out);
  and and_7 (Z, or_3_out, X);
  or or_5 (S_2, and_1_out, not_6_out, and_3_out);

  // Notes on the sheet:
  //   Z = X.(~Y + W)
  //   S = (A + B) .(~B + C)
  //   S = A.C + ~(B . C) + ~A . B . C
  //   S = A.B + ~C + ~(C.D)
endmodule
