// Logisim project Exercicio-3.circ as structural Verilog: 1 circuit, main circuit main
module main (
  input  A,
  input  B,
  output Primeira_casa,
  output Segunda_casa
);

  xor xor_1 (Primeira_casa, A, B);
  and and_1 (Segunda_casa, A, B);

  // Notes on the sheet:
  //   Soma de dois bits.
endmodule
