// Logisim project Exercicio-5.circ as structural Verilog
module Decodificador_2bits (
  input  in_1,
  input  in_2,
  output out_3,
  output out_4,
  output out_5,
  output out_6
);

  wire not_1_out, not_2_out, not_3_out, not_4_out;

  not not_1 (not_1_out, in_2);
  not not_2 (not_2_out, in_1);
  not not_3 (not_3_out, in_2);
  not not_4 (not_4_out, in_1);
  and and_1 (out_3, not_1_out, not_2_out);
  and and_2 (out_4, not_3_out, in_1);
  and and_3 (out_5, in_2, not_4_out);
  and and_4 (out_6, in_2, in_1);
endmodule

module Decodificador_3bits (
  input  A2,
  input  A1,
  input  A0,
  output S0,
  output S1,
  output S2,
  output S3,
  output S4,
  output S5,
  output S6,
  output S7
);

  wire not_1_out, not_2_out, not_3_out, not_4_out, not_5_out, not_6_out, not_7_out, not_8_out, not_9_out,
       not_10_out, not_11_out, not_12_out;

  not not_1 (not_1_out, A0);
  not not_2 (not_2_out, A1);
  not not_3 (not_3_out, A2);
  not not_4 (not_4_out, A1);
  not not_5 (not_5_out, A2);
  not not_6 (not_6_out, A0);
  not not_7 (not_7_out, A2);
  not not_8 (not_8_out, A2);
  not not_9 (not_9_out, A0);
  not not_10 (not_10_out, A1);
  not not_11 (not_11_out, A1);
  not not_12 (not_12_out, A0);
  and and_1 (S0, not_1_out, not_2_out, not_3_out);
  and and_2 (S1, A0, not_4_out, not_5_out);
  and and_3 (S2, not_6_out, A1, not_7_out);
  and and_4 (S3, A0, A1, not_8_out);
  and and_5 (S4, not_9_out, not_10_out, A2);
  and and_6 (S5, A0, not_11_out, A2);
  and and_7 (S6, not_12_out, A1, A2);
  and and_8 (S7, A0, A1, A2);
endmodule

module Decodificadores_logisim (
  input  [1:0] in_1,
  input  [2:0] in_2,
  output out_3,
  output out_4,
  output out_5,
  output out_6,
  output out_7,
  output out_8,
  output out_9,
  output out_10,
  output out_11,
  output out_12,
  output out_13,
  output out_14
);

  Decoder #(.select(2)) decoder_1 (.out0(out_3), .out1(out_4), .out2(out_5), .out3(out_6), .sel(in_1));  // open: en
  Decoder #(.select(3)) decoder_2 (
    .out0(out_7), .out1(out_8), .out2(out_9), .out3(out_10), .out4(out_11), .out5(out_12), .out6(out_13),
    .out7(out_14), .sel(in_2));  // open: en
endmodule
