// Logisim project Exercicios-4.circ as structural Verilog: 5 circuits, main circuit main
module main (
  input  [3:0] in_1,
  input  [3:0] in_2,
  output [3:0] out_3
);

  Adder #(.width(4)) adder_1 (.a(in_1), .b(in_2), .out(out_3));  // open: cin, cout
endmodule

module Somador_Completo (
  input  A,
  input  B,
  input  Carry_In,
  output Carry_On,
  output S
);

  wire and_1_out, and_2_out, xor_1_out;

  xor xor_1 (xor_1_out, A, B);
  and and_1 (and_1_out, B, A);
  and and_2 (and_2_out, Carry_In, xor_1_out);
  xor xor_2 (S, Carry_In, xor_1_out);
  or or_1 (Carry_On, and_1_out, and_2_out);
endmodule

module Somador_de_4bits (
  input  B3,
  input  B2,
  input  B1,
  input  B0,
  input  A3,
  input  A2,
  input  A1,
  input  A0,
  input  Carry_In,
  output Carry_Out,
  output S3,
  output S2,
  output S1,
  output S0
);

  wire somador_completo_2_carry_on, somador_completo_3_carry_on, somador_completo_4_carry_on;

  Somador_Completo somador_completo_1 (
    .Carry_On(Carry_Out), .A(B3), .S(S3), .B(A3), .Carry_In(somador_completo_2_carry_on));
  Somador_Completo somador_completo_2 (
    .Carry_On(somador_completo_2_carry_on), .A(B2), .S(S2), .B(A2), .Carry_In(somador_completo_3_carry_on));
  Somador_Completo somador_completo_3 (
    .Carry_On(somador_completo_3_carry_on), .A(B1), .S(S1), .B(A1), .Carry_In(somador_completo_4_carry_on));
  Somador_Completo somador_completo_4 (
    .Carry_On(somador_completo_4_carry_on), .A(B0), .S(S0), .B(A0), .Carry_In(Carry_In));
endmodule

module Somador_de_8bits (
  input  B7,
  input  B6,
  input  B5,
  input  B4,
  input  B3,
  input  B2,
  input  B1,
  input  B0,
  input  A7,
  input  A6,
  input  A5,
  input  A4,
  input  A3,
  input  A2,
  input  A1,
  input  A0,
  input  Carry_In,
  output Carry_Out,
  output S7,
  output S6,
  output S5,
  output S4,
  output S3,
  output S2,
  output S1,
  output S0
);

  wire somador_de_4bits_2_carry_out;

  Somador_de_4bits somador_de_4bits_1 (
    .B3(B7), .B2(B6), .B1(B5), .B0(B4), .A3(A7), .A2(A6), .A1(A5), .A0(A4), .Carry_Out(Carry_Out),
    .Carry_In(somador_de_4bits_2_carry_out), .S3(S7), .S2(S6), .S1(S5), .S0(S4));
  Somador_de_4bits somador_de_4bits_2 (
    .B3(B3), .B2(B2), .B1(B1), .B0(B0), .A3(A3), .A2(A2), .A1(A1), .A0(A0),
    .Carry_Out(somador_de_4bits_2_carry_out), .Carry_In(Carry_In), .S3(S3), .S2(S2), .S1(S1), .S0(S0));
endmodule

module Meio_Somador (
  input  A,
  input  B,
  output Carry_Out,
  output S
);

  and and_1 (Carry_Out, A, B);
  xor xor_1 (S, A, B);
endmodule
